// Logisim project D8421+5.circ as structural Verilog: 1 circuit, main circuit main
// 10unsigned
module main (
  input  [3:0] D8421,
  output [3:0] D8421_5
);

  wire and_1_out, and_2_out, and_3_out, and_4_out, and_5_out, and_6_out, and_7_out, and_8_out, and_9_out,
       and_10_out, and_11_out, and_12_out, and_13_out, not_1_out, not_2_out, not_3_out, not_4_out, not_5_out,
       not_6_out, not_7_out, not_8_out, not_9_out, not_10_out, not_11_out, not_12_out, not_13_out,
       not_14_out, not_15_out, not_16_out, not_17_out, not_18_out, not_19_out, not_20_out, not_21_out,
       not_22_out, not_23_out;

  // Probe on D8421
  not not_1 (not_1_out, D8421[0]);
  not not_2 (not_2_out, D8421[2]);
  not not_3 (not_3_out, D8421[0]);
  not not_4 (not_4_out, D8421[3]);
  not not_5 (not_5_out, D8421[1]);
  not not_6 (not_6_out, D8421[2]);
  not not_7 (not_7_out, D8421[2]);
  not not_8 (not_8_out, D8421[0]);
  not not_9 (not_9_out, D8421[3]);
  not not_10 (not_10_out, D8421[1]);
  not not_11 (not_11_out, D8421[3]);
  not not_12 (not_12_out, D8421[0]);
  not not_13 (not_13_out, D8421[3]);
  not not_14 (not_14_out, D8421[2]);
  not not_15 (not_15_out, D8421[0]);
  not not_16 (not_16_out, D8421[2]);
  not not_17 (not_17_out, D8421[1]);
  not not_18 (not_18_out, D8421[3]);
  not not_19 (not_19_out, D8421[2]);
  not not_20 (not_20_out, D8421[0]);
  not not_21 (not_21_out, D8421[2]);
  not not_22 (not_22_out, D8421[0]);
  not not_23 (not_23_out, D8421[3]);
  and and_1 (and_1_out, not_1_out, not_2_out);
  and and_2 (and_2_out, not_3_out, not_4_out);
  and and_3 (and_3_out, not_5_out, not_6_out, D8421[0]);
  and and_4 (and_4_out, not_7_out, D8421[1], not_8_out);
  and and_5 (and_5_out, not_9_out, not_10_out, D8421[0]);
  and and_6 (and_6_out, not_11_out, D8421[1], not_12_out);
  and and_7 (and_7_out, not_13_out, D8421[2], D8421[1], D8421[0]);
  and and_8 (and_8_out, not_14_out, not_15_out);
  and and_9 (and_9_out, not_16_out, not_17_out);
  and and_10 (and_10_out, D8421[0], D8421[1], not_18_out);
  and and_11 (and_11_out, D8421[3], not_19_out, not_20_out);
  and and_12 (and_12_out, D8421[3], not_21_out, not_22_out);
  and and_13 (and_13_out, not_23_out, D8421[2]);
  or or_1 (D8421_5[0], and_1_out, and_2_out);
  or or_2 (D8421_5[1], and_3_out, and_4_out, and_5_out, and_6_out);
  or or_3 (D8421_5[2], and_7_out, and_8_out, and_9_out);
  or or_4 (D8421_5[3], and_10_out, and_11_out, and_12_out, and_13_out);
  // Probe on D8421_5
endmodule
