// Logisim project LabWork5Scieme.circ as structural Verilog: 1 circuit, main circuit main
module main (
  input  V,
  output q3,
  output q2,
  output q1
);

  wire and_1_out, and_2_out, clock_1_out;

  and and_1 (and_1_out, V, q2, q1);
  and and_2 (and_2_out, V, q1);
  Clock clock_1 (.out(clock_1_out));
  T_Flip_Flop u_Q3 (.clk(clock_1_out), .T(and_1_out), .Q(q3));  // open: Qn, preset, reset, en
  T_Flip_Flop u_Q2 (.clk(clock_1_out), .T(and_2_out), .Q(q2));  // open: Qn, preset, reset, en
  T_Flip_Flop u_Q1 (.clk(clock_1_out), .T(V), .Q(q1));  // open: Qn, preset, reset, en
endmodule
